# Fritzing sketch serial_hoverboard_example_schematic (saved by Fritzing 0.9.3b)
breadboards: 1

parts:
  Bauteil1 = Arduino Uno (Rev3) - ICSP
  Bauteil2 = I2C level shifter bidirectional  # not connected
  Bauteil3 = Thumb Joystick

nets:
  N1: Bauteil1.A0, Bauteil3.HORZ
  N2: Bauteil1.A1, Bauteil3.VERT
  5V: Bauteil1.5V, Bauteil3.VCC
  GND: Bauteil1.GND, Bauteil3.GND

notes:
  Zu GND, RX, TX von UART am Mainboard
